// Logisim project Team 102.circ as structural Verilog: 3 circuits, main circuit ALU circuit
// AR
module main (
  input  in_1,
  input  in_2,
  input  in_3,
  input  in_4,
  input  in_5,
  input  [15:0] in_6,
  input  [15:0] in_7,
  input  in_8
);

  wire clock_1_out, controle_circuit_1_ac_enable, controle_circuit_1_ar_enable, controle_circuit_1_dr,
       controle_circuit_1_ir_enable, controle_circuit_1_memory_read, controle_circuit_1_memory_write,
       controle_circuit_1_pc_enable, controle_circuit_1_pc_inc, or_1_out, undriven;
  wire [2:0] controle_circuit_1_alu_selector, controle_circuit_1_bus_selector;
  wire [6:0] AR_q, bit_extender_1_out, bit_extender_2_out, PC_q;
  wire [15:0] AC_q, ALU_output_of_alu, bit_extender_3_out, bit_extender_4_out, DR_q, IR_q, multiplexer_1_out,
       ram_1_data, TR_q;

  Clock clock_1 (.out(clock_1_out));
  Bit_Extender #(.in_width(16), .out_width(7)) bit_extender_1 (.in(multiplexer_1_out), .out(bit_extender_1_out));
  Register #(.width(7)) AR (
    .D(bit_extender_2_out), .en(controle_circuit_1_ar_enable), .Q(AR_q), .clk(clock_1_out));  // open: clr
  Bit_Extender #(.in_width(16), .out_width(7)) bit_extender_2 (.in(multiplexer_1_out), .out(bit_extender_2_out));
  Register #(.width(16)) TR (.D(multiplexer_1_out), .en(in_1), .Q(TR_q), .clk(clock_1_out));  // open: clr
  Register #(.width(16)) DR (
    .D(multiplexer_1_out), .en(controle_circuit_1_dr), .Q(DR_q), .clk(clock_1_out));  // open: clr
  Register #(.width(16)) AC (
    .D(ALU_output_of_alu), .en(controle_circuit_1_ac_enable), .Q(AC_q), .clk(clock_1_out));  // open: clr
  Register #(.width(16)) IR (
    .D(multiplexer_1_out), .en(controle_circuit_1_ir_enable), .Q(IR_q), .clk(clock_1_out));  // open: clr
  Counter #(.width(7), .max('h7f)) PC (
    .load(controle_circuit_1_pc_enable), .D(bit_extender_1_out), .count(controle_circuit_1_pc_inc), .Q(PC_q),
    .clk(clock_1_out));  // open: carry, clr
  RAM #(.addrWidth(7), .dataWidth(16), .bus("separate")) ram_1 (
    .addr(AR_q), .din(multiplexer_1_out), .data(ram_1_data), .str(controle_circuit_1_memory_write),
    .clk(clock_1_out), .ld(controle_circuit_1_memory_read));  // open: sel, clr
  ALU_circuit ALU (
    .input1__DR(DR_q), .add_down(in_3), .sub_up(in_4), .add_up(in_2), .input_2_AC(AC_q), .sub_down(in_5),
    .mult_up(in_6), .mult_down(in_7), .Alu_seletive(controle_circuit_1_alu_selector), .inc_down(in_8),
    .output_of_ALU(ALU_output_of_alu));  // open: inc_up
  assign bit_extender_3_out = {{9{1'b0}}, AR_q};  // Bit_Extender bit_extender_3
  assign bit_extender_4_out = {{9{1'b0}}, PC_q};  // Bit_Extender bit_extender_4
  or or_1 (or_1_out, AC_q[0], AC_q[1], AC_q[2], AC_q[3], AC_q[4], AC_q[5], AC_q[6], AC_q[7], AC_q[8], AC_q[9], AC_q[10], AC_q[11], AC_q[12], AC_q[13], AC_q[14], AC_q[15]);
  controle_circuit controle_circuit_1 (
    .opcode(IR_q[14:12]), .IR_15(IR_q[15]), .IR_5(IR_q[5]), .clk(clock_1_out), .Z_AC(or_1_out),
    .memory_write(controle_circuit_1_memory_write), .bus_selector(controle_circuit_1_bus_selector),
    .DR(controle_circuit_1_dr), .AC_enable(controle_circuit_1_ac_enable),
    .PC_enable(controle_circuit_1_pc_enable), .PC_inc(controle_circuit_1_pc_inc),
    .IR_enable(controle_circuit_1_ir_enable), .AR_enable(controle_circuit_1_ar_enable),
    .memory_read(controle_circuit_1_memory_read), .ALU_SELECTOR(controle_circuit_1_alu_selector));  // open: in_5
  Multiplexer #(.select(3), .width(16)) multiplexer_1 (
    .in0(AC_q), .in1(DR_q), .in2(TR_q), .in3(bit_extender_3_out), .in4(ram_1_data), .in5(bit_extender_4_out),
    .in6(IR_q), .out(multiplexer_1_out), .sel(controle_circuit_1_bus_selector), .en(undriven));  // open: in7
endmodule

// controler
module controle_circuit (
  input  [2:0] opcode,
  input  IR_15,
  input  IR_5,
  input  clk,
  input  [3:0] in_5,
  input  Z_AC,
  output memory_write,
  output [2:0] bus_selector,
  output DR,
  output AC_enable,
  output PC_enable,
  output PC_inc,
  output IR_enable,
  output AR_enable,
  output memory_read,
  output [2:0] ALU_SELECTOR
);

  wire and_1_out, and_2_out, and_3_out, and_4_out, and_5_out, and_6_out, and_7_out, and_8_out, and_9_out,
       and_10_out, and_11_out, and_12_out, and_14_out, and_15_out, and_16_out, and_17_out, d_ff_1_q,
       decoder_1_out0, decoder_1_out1, decoder_1_out2, decoder_1_out3, decoder_1_out4, decoder_1_out5,
       decoder_1_out6, decoder_1_out7, decoder_2_out0, decoder_2_out2, decoder_2_out3, decoder_2_out4,
       decoder_2_out5, decoder_2_out6, not_1_out, not_2_out, not_3_out, not_4_out, or_1_out, or_2_out,
       SC_clear_out;
  wire [3:0] SC_q;

  Counter #(.width(4), .max('hf)) SC (
    .D(in_5), .count(not_1_out), .Q(SC_q), .clk(clk), .clr(d_ff_1_q));  // open: load, carry
  not not_1 (not_1_out, SC_clear_out);
  D_Flip_Flop d_ff_1 (.clk(clk), .D(SC_clear_out), .Q(d_ff_1_q));  // open: Qn, preset, en, reset
  Decoder #(.select(3)) decoder_1 (
    .out0(decoder_1_out0), .out1(decoder_1_out1), .out2(decoder_1_out2), .out3(decoder_1_out3),
    .out4(decoder_1_out4), .out5(decoder_1_out5), .out6(decoder_1_out6), .out7(decoder_1_out7), .sel(opcode));  // open: en
  Decoder #(.select(4)) decoder_2 (
    .out0(decoder_2_out0), .out1(IR_enable), .out2(decoder_2_out2), .out3(decoder_2_out3),
    .out4(decoder_2_out4), .out5(decoder_2_out5), .out6(decoder_2_out6), .sel(SC_q));  // open: out7, out8, out9, out10, out11, out12, out13, out14, out15, en
  not not_2 (not_2_out, decoder_1_out7);
  or or_1 (or_1_out, decoder_1_out0, decoder_1_out1, decoder_1_out2, decoder_1_out5, decoder_1_out6);
  and and_1 (and_1_out, or_1_out, decoder_2_out4);
  and and_2 (and_2_out, decoder_1_out6, decoder_2_out5);
  or or_2 (or_2_out, decoder_1_out0, decoder_1_out1, decoder_1_out2, decoder_1_out5);
  not not_3 (not_3_out, IR_15);
  not not_4 (not_4_out, Z_AC);
  or or_3 (DR, and_1_out, and_2_out);
  and and_3 (and_3_out, decoder_2_out5, or_2_out);
  and and_4 (and_4_out, decoder_1_out7, not_3_out, IR_5, decoder_2_out3);
  and and_5 (and_5_out, decoder_2_out6, decoder_1_out6, not_4_out);
  and and_6 (and_6_out, decoder_1_out2, decoder_2_out5);
  and and_7 (and_7_out, decoder_2_out5, decoder_1_out1);
  and and_8 (and_8_out, decoder_2_out5, decoder_1_out5);
  and and_9 (and_9_out, decoder_1_out0, decoder_2_out5);
  and and_10 (and_10_out, decoder_1_out6, decoder_2_out5);
  and and_11 (and_11_out, decoder_1_out6, decoder_2_out6);
  and and_12 (and_12_out, decoder_1_out3, decoder_2_out4);
  or or_4 (AC_enable, and_3_out, and_4_out);
  and and_13 (PC_enable, decoder_1_out4, decoder_2_out4);
  or or_5 (PC_inc, IR_enable, and_5_out);
  and and_14 (and_14_out, decoder_2_out3, not_2_out, IR_15);
  or or_6 (memory_write, and_11_out, and_12_out);
  or or_7 (AR_enable, decoder_2_out0, decoder_2_out2, and_14_out);
  Priority_Encoder priority_encoder_1 (
    .in1(and_6_out), .in2(and_7_out), .in3(and_8_out), .in4(and_9_out), .in5(and_10_out), .out(ALU_SELECTOR));  // open: in0, in6, in7, en_in, gs, en_out
  and and_15 (and_15_out, decoder_2_out4, decoder_1_out3);
  and and_16 (and_16_out, decoder_1_out6, decoder_2_out6);
  or or_8 (memory_read, IR_enable, and_14_out, and_1_out);
  and and_17 (and_17_out, decoder_2_out4, decoder_1_out4);
  Priority_Encoder priority_encoder_2 (
    .in0(and_15_out), .in3(and_17_out), .in4(memory_read), .in5(decoder_2_out0), .in6(decoder_2_out2),
    .out(bus_selector));  // open: in1, in2, in7, en_in, gs, en_out
  or SC_clear (SC_clear_out, memory_write, and_3_out, and_16_out);
endmodule

// ALU
module ALU_circuit (
  input  [15:0] input1__DR,
  input  add_down,
  input  sub_up,
  input  add_up,
  input  [15:0] input_2_AC,
  input  sub_down,
  input  [15:0] mult_up,
  input  [15:0] mult_down,
  input  inc_up,
  input  [2:0] Alu_seletive,
  input  inc_down,
  output [15:0] output_of_ALU
);

  wire [15:0] adder_1_out, adder_2_out, and_1_out, multiplier_1_out, or_1_out, subtractor_1_out;

  Adder #(.width(16)) adder_1 (.a(input1__DR), .b(input_2_AC), .out(adder_1_out), .cin(add_up), .cout(add_down));
  Subtractor #(.width(16)) subtractor_1 (
    .a(input_2_AC), .b(input1__DR), .out(subtractor_1_out), .bin(sub_up), .bout(sub_down));
  Multiplier #(.width(16)) multiplier_1 (
    .a(input1__DR), .b(input_2_AC), .out(multiplier_1_out), .cin(mult_up), .cout(mult_down));
  Adder #(.width(16)) adder_2 (.a(input1__DR), .b(16'h1), .out(adder_2_out), .cin(inc_up), .cout(inc_down));
  assign or_1_out = input1__DR | input_2_AC;  // OR_Gate or_1, 16 bits wide
  assign and_1_out = input1__DR & input_2_AC;  // AND_Gate and_1, 16 bits wide
  Multiplexer #(.select(3), .width(16)) multiplexer_1 (
    .in1(input1__DR), .in2(adder_1_out), .in3(subtractor_1_out), .in4(multiplier_1_out), .in5(adder_2_out),
    .in6(or_1_out), .in7(and_1_out), .out(output_of_ALU), .sel(Alu_seletive));  // open: in0, en
endmodule
